// Logisim project interrupt_controller.circ as structural Verilog: 1 circuit, main circuit main
module main (
  input  RST,
  input  in_2,
  input  in_3,
  input  in_4,
  input  in_5,
  input  in_6,
  input  in_7,
  input  in_8,
  input  gie_mask,
  input  in_10,
  input  k0_0,
  input  in_12,
  input  in_13,
  input  in_14
);

  wire and_7_out, and_8_out, and_9_out, and_10_out, CLK, clr_irq_s_0, d_ff_2_q, d_ff_3_q, d_ff_4_q, d_ff_5_q,
       d_ff_6_q, d_ff_7_q, d_ff_8_q, d_ff_9_q, d_ff_10_q, decoder_1_out2, FIRIF7, GIE, ifg_s_0, INT1, INT2,
       INT3, INT4, INT5, INT6, INTR, irq_s_0, is_interrupt_s, not_1_out, not_2_out, not_3_out, or_1_out,
       or_5_out, undriven_2, undriven_3, undriven_4;
  wire [3:0] enc_pri_int_s, SELECTED_SYNC_INY;
  wire [7:0] controlled_buffer_1_out, type_reg_d_in, TYPE_REG_q, undriven;

  not not_1 (not_1_out, GIE);
  Decoder #(.select(4)) decoder_1 (
    .out0(clr_irq_s_0), .out2(decoder_1_out2), .sel(SELECTED_SYNC_INY), .en(not_1_out));  // open: out1, out3, out4, out5, out6, out7, out8, out9, out10, out11, out12, out13, out14, out15
  D_Flip_Flop d_ff_1 (.D(1'b1), .Q(irq_s_0), .reset(or_1_out));  // open: clk, Qn, preset
  or or_1 (or_1_out, RST, clr_irq_s_0);
  D_Flip_Flop d_ff_2 (.D(1'b1), .Q(d_ff_2_q), .reset(decoder_1_out2));  // open: clk, Qn, preset
  D_Flip_Flop d_ff_3 (.D(1'b1), .Q(d_ff_3_q));  // open: clk, Qn, preset, reset
  D_Flip_Flop d_ff_4 (.D(1'b1), .Q(d_ff_4_q));  // open: clk, Qn, preset, reset
  D_Flip_Flop d_ff_5 (.D(1'b1), .Q(d_ff_5_q));  // open: clk, Qn, preset, reset
  D_Flip_Flop d_ff_6 (.D(1'b1), .Q(d_ff_6_q));  // open: clk, Qn, preset, reset
  D_Flip_Flop d_ff_7 (.D(1'b1), .Q(d_ff_7_q));  // open: clk, Qn, preset, reset
  D_Flip_Flop d_ff_8 (.D(1'b1), .Q(d_ff_8_q));  // open: clk, Qn, preset, reset
  D_Flip_Flop d_ff_9 (.D(1'b1), .Q(d_ff_9_q));  // open: clk, Qn, preset, reset
  D_Flip_Flop d_ff_10 (.D(1'b1), .Q(d_ff_10_q));  // open: clk, Qn, preset, reset
  Clock clock_1 (.out(CLK));
  and and_1 (ifg_s_0, irq_s_0, in_6);
  and and_2 (INT1, d_ff_2_q, in_3);
  and and_3 (INT2, d_ff_3_q, in_4);
  and and_4 (INT3, d_ff_4_q, in_7);
  and and_5 (INT4, d_ff_5_q, in_8);
  and and_6 (INT5, d_ff_6_q, in_10);
  and and_7 (and_7_out, d_ff_7_q, in_12);
  and and_8 (and_8_out, d_ff_8_q, in_13);
  and and_9 (and_9_out, d_ff_9_q, in_14);
  and and_10 (and_10_out, d_ff_10_q, in_14);
  Register IFG_REG (.D(undriven));  // open: en, clk, Q, clr
  or or_2 (FIRIF7, and_9_out, and_10_out);
  or or_3 (INT6, and_7_out, and_8_out);
  or or_4 (is_interrupt_s, ifg_s_0, INT1, INT2, INT3, INT4, INT5, and_7_out, and_8_out, and_9_out, and_10_out);
  and and_11 (INTR, is_interrupt_s, GIE);
  Priority_Encoder #(.select(4)) priority_encoder_1 (
    .in0(undriven_2), .in1(undriven_3), .in3(undriven_4), .out(enc_pri_int_s));  // open: in2, in4, in5, in6, in7, in8, in9, in10, in11, in12, in13, in14, in15, gs, en_out, en_in
  Register #(.width(4)) register_1 (.D(enc_pri_int_s), .en(1'b1), .clk(not_2_out), .Q(SELECTED_SYNC_INY));  // open: clr
  not not_2 (not_2_out, in_2);
  Multiplexer #(.select(4), .width(8)) multiplexer_1 (
    .in0({8{1'b0}}), .in1(8'h4), .out(type_reg_d_in), .sel(SELECTED_SYNC_INY));  // open: in2, in3, in4, in5, in6, in7, in8, in9, in10, in11, in12, in13, in14, in15
  and and_12 (GIE, gie_mask, k0_0);
  not not_3 (not_3_out, GIE);
  Register TYPE_REG (.D(type_reg_d_in), .en(1'b1), .clk(not_3_out), .Q(TYPE_REG_q));  // open: clr
  assign controlled_buffer_1_out = or_5_out ? TYPE_REG_q : 8'bz;  // Controlled_Buffer controlled_buffer_1
  or or_5 (or_5_out, in_5, 1'b0);

  // Other names for the same wires on the sheet: en_int_s_0 = in_6; INT0 = ifg_s_0; INTA = in_2; TYPE_INT_OUT = in_5
endmodule
